# Fritzing sketch prog_adaptor (saved by Fritzing 0.7.11b)
breadboards: 1

parts:
  IC1 = ATMega8 [package=DIL]
  IC2 = AVRISP [package=SIL]
  R1 = Resistor [tolerance=±5% resistance=10k package=THT]
  Y1 = Resonator [frequency="8 MHz" package=THT]

nets:
  N1: IC1.RESET/PC6, IC2.RST, R1.Pin_1
  VCC: IC1.VCC, IC2.VCC, R1.Pin_0
  GND: IC1.GND, IC2.GND#7, Y1.GND
  N2: IC1.XTAL1/TOSC1/PB6, Y1.0
  N3: IC1.XTAL2/TOSC2/PB7, Y1.pin_1
  N4: IC1.MOSI/OC2/PB3, IC2.MOSI
  N5: IC1.MISO/PB4, IC2.MISO
  N6: IC1.SCK/PB5, IC2.SCK

notes:
  AVR ISP Programming Harness, AVR ISP Programming Adaptor, 1F
